# Fritzing sketch line follower diagram (saved by Fritzing 0.9.3b)
breadboards: 1

parts:
  M1 = DC Motor
  M2 = DC Motor
  M3 = DC Motor
  M4 = DC Motor
  S1 = H-Bridge with L298N
  Part1 = Arduino Uno (Rev3)
  RIGHT = Keyes IR Infrared Sensor Switch Module
  LEFT = Keyes IR Infrared Sensor Switch Module
  BATT1 = LiPoly Battery (1300mAh)

nets:
  N1: M1.pin_1, M2.pin_1, S1.M2-02
  N2: M1.pin_2, M2.pin_2, S1.M2-01
  N3: M3.pin_1, M4.pin_1, S1.M1-02
  N4: M3.pin_2, M4.pin_2, S1.M1-01
  N5: S1.12V, BATT1.positive
  N6: S1.GND, BATT1.negative
  5V: S1.5V, Part1.VIN
  N7: S1.ENA, Part1.D8
  N8: S1.IN1, Part1.D6_PWM
  N9: S1.IN2, Part1.D5_PWM
  N10: S1.IN3, Part1.D9_PWM
  N11: S1.IN4, Part1.D10_PWM/SS
  N12: S1.ENB, Part1.D7
  N13: Part1.D3_PWM, RIGHT.out
  N14: Part1.D4, LEFT.out
  3V3: Part1.3V3, LEFT.VCC
  GND: Part1.GND, LEFT.GND

custom parts:
  H-Bridge with L298N: h-bridge
  Keyes IR Infrared Sensor Switch Module: An infrared obstacle detector
  LiPoly Battery (1300mAh): Lithium Ion Polymer Battery (1300mAh)
